# Fritzing sketch WetterObservatoriumESP8266 (saved by Fritzing 0.9.2b)
circuit board: 10.1705cm x 6.62831cm
stripboards: 2

parts:
  Pulldown_Widerstand = Resistor [tolerance=±5% resistance=10k package=THT]
  DHT22 = DHT22 Humidity and Temperature Sensor
  Fotowiderstand = Photocell (LDR) [package=THT]
  part = NodeMCU V3.0
  BMP280 = Adafruit BME280

nets:
  GND: Pulldown_Widerstand.Pin_0, DHT22.GND, part.GND, BMP280.GND
  N1: Pulldown_Widerstand.Pin_1, Fotowiderstand.pin_0, part.A0
  VDD: DHT22.VDD, Fotowiderstand.pin_1, part.3V3, BMP280.VIN
  N2: DHT22.DATA, part.D5
  N3: part.D1, BMP280.SCK/SCL
  N4: part.D2, BMP280.SDI/SDA

custom parts:
  NodeMCU V3.0: ESP8266 based NodeMCU
  Adafruit BME280: Bosch has stepped up their game with their new BME280 sensor, an environmental sensor with temperature, barometric pressure and humidity! This sensor is great for all sorts of weather/environmental sensing and can even be used in both I2C and SPI! This precision sensor from Bosch is the best low-cost sensing solution for measuring humidity with ±3% accuracy, barometric pressure with ±1 hPa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
